# Fritzing sketch NistkastenV2 (saved by Fritzing 0.9.3b)

parts:
  RHT1 = Humidity and Temperature Sensor RHT03
  Raspberry_Pi_Zero1 = Raspberry Pi Zero
  R1 = Resistor [tolerance=±5% resistance=220 package="2010 [SMD]"]

nets:
  N1: RHT1.Data-signal, Raspberry_Pi_Zero1.GPIO4
  N2: RHT1.GND_2, Raspberry_Pi_Zero1.GND
  N3: Raspberry_Pi_Zero1.3v3, R1.Pin_0

notes:
  Zum Netzteil
  +
  -
